# Fritzing sketch schema script (saved by Fritzing 0.8.7b)
breadboards: 1

parts:
  Composant1 = Arduino Uno (Rev3)
  R1 = Resistor [tolerance=±5% resistance=330 package=THT]
  LED1 = LED - 3mm [color="Red (633nm)" package="3 mm [THT]"]

nets:
  N1: Composant1.D9_PWM, LED1.anode
  N2: Composant1.GND, R1.Pin_0
  N3: R1.Pin_1, LED1.cathode
